// Logisim project assignment2.circ as structural Verilog
module main (
  input  in_1,
  input  in_2,
  input  in_3,
  input  in_4,
  input  [7:0] in_5,
  input  [2:0] in_6,
  input  [2:0] in_7,
  input  in_8,
  output out_9,
  output out_10,
  output out_11
);

  wire vote25_1_result;
  wire [7:0] count_led_1_display, letters_1_display;
  wire [14:0] dipswitch_1_sw15;
  wire [24:0] dipswitch_2_p24;

  DipSwitch #(.number(15)) dipswitch_1 (
    .sw1(dipswitch_1_sw15[14]), .sw2(dipswitch_1_sw15[13]), .sw3(dipswitch_1_sw15[12]),
    .sw4(dipswitch_1_sw15[11]), .sw5(dipswitch_1_sw15[10]), .sw6(dipswitch_1_sw15[9]),
    .sw7(dipswitch_1_sw15[8]), .sw8(dipswitch_1_sw15[7]), .sw9(dipswitch_1_sw15[6]),
    .sw10(dipswitch_1_sw15[5]), .sw11(dipswitch_1_sw15[4]), .sw12(dipswitch_1_sw15[3]),
    .sw13(dipswitch_1_sw15[2]), .sw14(dipswitch_1_sw15[1]), .sw15(dipswitch_1_sw15[0]));
  and_or4 and_or4_1 (.a(in_1), .b(in_2), .c(in_3), .d(in_4), .out1(out_9), .out2(out_10));
  mux8_1 mux8_1_1 (.d(in_5), .ch(in_6), .data(out_11));
  // DipSwitch #(.number(25)) dipswitch_2: pin names not known; wires that end beside it: dipswitch_2_p24[23], dipswitch_2_p24[22], dipswitch_2_p24[21], dipswitch_2_p24[20], dipswitch_2_p24[19], dipswitch_2_p24[18], dipswitch_2_p24[17], dipswitch_2_p24[16], dipswitch_2_p24[15], dipswitch_2_p24[14], dipswitch_2_p24[13], dipswitch_2_p24[12], dipswitch_2_p24[11], dipswitch_2_p24[10], dipswitch_2_p24[9], dipswitch_2_p24[8], dipswitch_2_p24[7], dipswitch_2_p24[6], dipswitch_2_p24[5], dipswitch_2_p24[4], dipswitch_2_p24[3], dipswitch_2_p24[2], dipswitch_2_p24[1], dipswitch_2_p24[0]
  letters letters_1 (.sel(in_7), .display(letters_1_display));
  _7_Segment_Display u_7_segment_display_1 (
    .g(letters_1_display[1]), .f(letters_1_display[2]), .a(letters_1_display[7]), .b(letters_1_display[6]),
    .e(letters_1_display[3]), .d(letters_1_display[4]), .c(letters_1_display[5]), .dp(letters_1_display[0]));
  count_led count_led_1 (.en(in_8), .vt(dipswitch_1_sw15), .display(count_led_1_display));
  _7_Segment_Display u_7_segment_display_2 (
    .g(count_led_1_display[1]), .f(count_led_1_display[2]), .a(count_led_1_display[7]),
    .b(count_led_1_display[6]), .e(count_led_1_display[3]), .d(count_led_1_display[4]),
    .c(count_led_1_display[5]), .dp(count_led_1_display[0]));
  vote25 vote25_1 (.vt(dipswitch_2_p24), .result(vote25_1_result));
  LED led_1 (.in(vote25_1_result));
endmodule

// VHDL entity and_or4, as the project stores it:
library ieee;
use ieee.std_logic_1164.all;

entity and_or4 is
    port (
        a, b, c, d : in std_logic;
        out1, out2 : out std_logic
    );
end entity and_or4;

architecture bhv of and_or4 is
begin
    out1 <= a and b and c and d;
    out2 <= a or b or c or d;
end architecture bhv;

// VHDL entity mux8_1, as the project stores it:
library ieee;
use ieee.std_logic_1164.all;

entity mux8_1 is
    port (
        d    : in  std_logic_vector(7 downto 0);
        ch   : in  std_logic_vector(2 downto 0);
        data : out std_logic
    );
end entity mux8_1;

architecture bhv of mux8_1 is
begin
    process(d, ch)
    begin
        case ch is
            when "000" => data <= d(0);
            when "001" => data <= d(1);
            when "010" => data <= d(2);
            when "011" => data <= d(3);
            when "100" => data <= d(4);
            when "101" => data <= d(5);
            when "110" => data <= d(6);
            when "111" => data <= d(7);
            when others => data <= '0';
        end case;
    end process;
end architecture bhv;

// VHDL entity letters, as the project stores it:
library ieee;
use ieee.std_logic_1164.all;

entity letters is
    port (
        sel     : in  std_logic_vector(2 downto 0);
        display : out std_logic_vector(7 downto 0)
    );
end entity letters;

architecture bhv of letters is
begin
    process(sel)
    begin
        case sel is
            when "000" => display <= "11101110"; -- A
            when "001" => display <= "00111110"; -- b
            when "010" => display <= "10011100"; -- C
            when "011" => display <= "01111010"; -- d
            when "100" => display <= "10001110"; -- F
            when "101" => display <= "11110110"; -- G
            when others => display <= "00000000";
        end case;
    end process;
end architecture bhv;

// VHDL entity vote25, as the project stores it:
library ieee;
use ieee.std_logic_1164.all;

entity vote25 is
    port (
        vt     : in  std_logic_vector(25 downto 1);
        result : out std_logic
    );
end entity vote25;

architecture bhv of vote25 is
begin
    process(vt)
        variable sum : integer range 0 to 25;
    begin
        sum := 0;
        for i in 1 to 25 loop
            if vt(i) = '1' then
                sum := sum + 1;
            end if;
        end loop;
        if sum >= 13 then
            result <= '1';
        else
            result <= '0';
        end if;
    end process;
end architecture bhv;

// VHDL entity count_led, as the project stores it:
library ieee;
use ieee.std_logic_1164.all;

entity count_led is
    port (
        en      : in  std_logic;
        vt      : in  std_logic_vector(15 downto 1);
        display : out std_logic_vector(7 downto 0)
    );
end entity count_led;

architecture bhv of count_led is
begin
    process(en, vt)
        variable sum : integer range 0 to 15;
    begin
        sum := 0;
        for i in 1 to 15 loop
            if vt(i) = '1' then
                sum := sum + 1;
            end if;
        end loop;

        if en = '0' then
            display <= "00000000";
        else
            case sum is
                when 0  => display <= "11111100";
                when 1  => display <= "01100000";
                when 2  => display <= "11011010";
                when 3  => display <= "11110010";
                when 4  => display <= "01100110";
                when 5  => display <= "10110110";
                when 6  => display <= "10111110";
                when 7  => display <= "11100000";
                when 8  => display <= "11111110";
                when 9  => display <= "11100110";
                when 10 => display <= "11101110"; -- A
                when 11 => display <= "00111110"; -- b
                when 12 => display <= "10011100"; -- C
                when 13 => display <= "01111010"; -- d
                when 14 => display <= "10011110"; -- E
                when 15 => display <= "10001110"; -- F
                when others => display <= "00000000";
            end case;
        end if;
    end process;
end architecture bhv;
